# Fritzing sketch Wiring Diagram (saved by Fritzing 1.0.6)
breadboards: 1

parts:
  R1 = Resistor [tolerance=±5% power=0.25W resistance=220 package=THT]
  C1 = Electrolytic Capacitor [capacitance=0.47mF voltage=35V package="100 mil [THT, electrolytic]"]
  Mod1 = Heltec WiFi LoRa 32 V2 [part_number=HTIT-WB32LA]
  HC-SR04_Sensor_1 = HC-SR04 Ultrasonic Distance Sensor
  S1 = Tilt Switch [package=THT]
  J1 = Basic Servo
  S2 = Toggle Switch [package=THT]
  LED1 = LED - 5mm [color="Red (633nm)" current=0.030A package="5 mm [THT]"]
  MOD1 = MT3608 Boost No usb
  BAT1 = 18650 battery holder [package=battery-18650-kit]
  R2 = Resistor [tolerance=±5% power=0.25W resistance=1k package=THT]
  R3 = Resistor [tolerance=±5% power=0.25W resistance=2k package=THT]

nets:
  N1: R1.Pin_0, LED1.anode
  N2: R1.Pin_1, Mod1.pin_4
  GND: C1.-, Mod1.GND, HC-SR04_Sensor_1.GND, S1.Pin_2, J1.gnd, LED1.cathode, MOD1.IN_(-), MOD1.OUT_(-), BAT1.+, R3.Pin_0
  VCC: C1.+, HC-SR04_Sensor_1.VCC, J1.vcc, MOD1.OUT_(+)
  N3: Mod1.pin_2, S1.Pin_1
  N4: Mod1.pin_3, J1.pulse
  N5: Mod1.pin_16, Mod1.pin_17, S2.L2, MOD1.IN_(+)
  N6: Mod1.pin_21, Mod1.pin_22
  N7: Mod1.pin_35, HC-SR04_Sensor_1.TRIG
  N8: Mod1.pin_36, R2.Pin_0, R3.Pin_1
  N9: HC-SR04_Sensor_1.ECHO, R2.Pin_1
  N10: S2.COM, BAT1.-

custom parts:
  MT3608 Boost No usb: Chip- MT3608 / B6289 DC to DC step up, power booster module. With adjustable output voltage. Current- 2A . || Input voltage- 2V-24V || Output voltage- 5V-28V Input interface- Inversed polarity- NO. || Led indicator- No.
  18650 battery holder: 18650 Battery Holder identical to the dual battery version.
